# Fritzing sketch CapteurDeMouvement (saved by Fritzing 0.9.0b)
circuit board: 8.46667cm x 5.64444cm
breadboards: 1

parts:
  TRINKET1 = Trinket 5V
  LED1 = smd LED [color="Red (633nm)" package="0805 [SMD]"]
  PIR1 = PIR sensor
  U1 = RELAY [package=relay-g5q]

nets:
  N1: TRINKET1.no_name_yet#2, LED1.cathode, PIR1.GND, U1.COIL2
  N2: TRINKET1.no_name_yet#3, LED1.anode, U1.NC
  N3: TRINKET1.no_name_yet#6, PIR1.VDD, U1.COIL1
  N4: TRINKET1.no_name_yet#7, PIR1.SIG

custom parts:
  Trinket 5V: Adafruit Trinket 5V
